# Fritzing sketch Электрическая схема (saved by Fritzing 0.9.3b)

parts:
  Часть4 = Arduino Mega 2560 (Rev3)
  Часть6 = Bluetooth HC-05 Macho
  S1 = H-Bridge with L298N
  S2 = H-Bridge with L298N
  R1 = Resistor [tolerance=±5% resistance=220 package="0603 [SMD]"]
  R2 = Resistor [tolerance=±5% resistance=220 package="0603 [SMD]"]
  U3 = SWITCH_SPDT [package=kps-1290]
  U4 = SWITCH_SPDT [package=kps-1290]
  M1 = DC Motor
  M3 = DC Motor
  M2 = DC Motor

nets:
  N1: Часть4.D20/SDA, U4.O
  N2: Часть4.D19/RX1, U3.O
  N3: Часть4.D17_PWM/RX2, Часть6.TXD
  N4: Часть4.D16_PWM/TX2, Часть6.RXD
  GND: Часть4.GND, Часть6.GND, S1.GND, S2.GND, U3.P, U4.P
  N5: Часть4.D11_PWM, S2.IN4
  N6: Часть4.D10_PWM, S2.IN3
  N7: Часть4.D9_PWM, S1.IN4
  N8: Часть4.D8_PWM, S1.5V
  5V: Часть4.5V, Часть6.VCC, R1.Pin_1, R2.Pin_1
  12V: Часть4.VIN, S1.12V, S2.12V
  N9: Часть4.D3_PWM, S1.IN3
  N10: Часть4.D5_PWM, S2.IN1
  N11: Часть4.D6_PWM, S2.IN2
  N12: Часть4.D7_PWM, S2.5V
  N13: S1.M1-01, M3.pin_2
  N14: S1.M1-02, M3.pin_1
  N15: S2.M1-01, M2.pin_2
  N16: S2.M1-02, M2.pin_1
  N17: S2.M2-01, M1.pin_1
  N18: S2.M2-02, M1.pin_2

custom parts:
  H-Bridge with L298N: h-bridge
